# Fritzing sketch neopixel-globe-4 (saved by Fritzing 0.9.3b)
circuit board: 10.0013cm x 10.0013cm
breadboards: 1

parts:
  1000_uf = Electrolytic Capacitor [capacitance=1mF voltage=35V part_number="1000uF 25V 85C" package="200 mil [THT, electrolytic]"]
  R330 = Resistor [tolerance=±5% resistance=330 part_number=330 package=THT]
  Raspberry_Pi_Zero1 = Raspberry Pi Zero
  J1 = female pin header, 4 pins [form="♀ (female)"]
  J2 = female pin header, 4 pins [form="♀ (female)"]
  J3 = female pin header, 4 pins [form="♀ (female)"]
  J4 = female pin header, 4 pins [form="♀ (female)"]
  J5 = female pin header, 4 pins [form="♀ (female)"]
  J6 = female pin header, 4 pins [form="♀ (female)"]
  J7 = female pin header, 4 pins [form="♀ (female)"]
  J8 = female pin header, 4 pins [form="♀ (female)"]
  J9 = female pin header, 4 pins [form="♀ (female)"]
  J10 = female pin header, 4 pins [form="♀ (female)"]
  J11 = female pin header, 4 pins [form="♀ (female)"]
  J12 = female pin header, 4 pins [form="♀ (female)"]
  J13 = female pin header, 4 pins [form="♀ (female)"]
  J14 = female pin header, 4 pins [form="♀ (female)"]
  J15 = female pin header, 4 pins [form="♀ (female)"]
  J16 = female pin header, 4 pins [form="♀ (female)"]
  J17 = female pin header, 4 pins [form="♀ (female)"]
  J18 = female pin header, 4 pins [form="♀ (female)"]
  J19 = female pin header, 4 pins [form="♀ (female)"]
  J20 = female pin header, 4 pins [form="♀ (female)"]
  J21 = female pin header, 4 pins [form="♀ (female)"]
  J22 = female pin header, 4 pins [form="♀ (female)"]
  J23 = female pin header, 4 pins [form="♀ (female)"]
  J24 = female pin header, 4 pins [form="♀ (female)"]
  C18 = Ceramic Capacitor [capacitance=100nF voltage=6.3V package="200 mil [THT, multilayer]"]
  C1 = Ceramic Capacitor [capacitance=100nF voltage=6.3V package="200 mil [THT, multilayer]"]
  C2 = Ceramic Capacitor [capacitance=100nF voltage=6.3V package="200 mil [THT, multilayer]"]
  C19 = Ceramic Capacitor [capacitance=100nF voltage=6.3V package="200 mil [THT, multilayer]"]
  C20 = Ceramic Capacitor [capacitance=100nF voltage=6.3V package="200 mil [THT, multilayer]"]
  C21 = Ceramic Capacitor [capacitance=100nF voltage=6.3V package="200 mil [THT, multilayer]"]
  C22 = Ceramic Capacitor [capacitance=100nF voltage=6.3V package="200 mil [THT, multilayer]"]
  C23 = Ceramic Capacitor [capacitance=100nF voltage=6.3V package="200 mil [THT, multilayer]"]
  C24 = Ceramic Capacitor [capacitance=100nF voltage=6.3V package="200 mil [THT, multilayer]"]
  C3 = Ceramic Capacitor [capacitance=100nF voltage=6.3V package="200 mil [THT, multilayer]"]
  C4 = Ceramic Capacitor [capacitance=100nF voltage=6.3V package="200 mil [THT, multilayer]"]
  C5 = Ceramic Capacitor [capacitance=100nF voltage=6.3V package="200 mil [THT, multilayer]"]
  C6 = Ceramic Capacitor [capacitance=100nF voltage=6.3V package="200 mil [THT, multilayer]"]
  C7 = Ceramic Capacitor [capacitance=100nF voltage=6.3V package="200 mil [THT, multilayer]"]
  C8 = Ceramic Capacitor [capacitance=100nF voltage=6.3V package="200 mil [THT, multilayer]"]
  C9 = Ceramic Capacitor [capacitance=100nF voltage=6.3V package="200 mil [THT, multilayer]"]
  C10 = Ceramic Capacitor [capacitance=100nF voltage=6.3V package="200 mil [THT, multilayer]"]
  C11 = Ceramic Capacitor [capacitance=100nF voltage=6.3V package="200 mil [THT, multilayer]"]
  C12 = Ceramic Capacitor [capacitance=100nF voltage=6.3V package="200 mil [THT, multilayer]"]
  C13 = Ceramic Capacitor [capacitance=100nF voltage=6.3V package="200 mil [THT, multilayer]"]
  C14 = Ceramic Capacitor [capacitance=100nF voltage=6.3V package="200 mil [THT, multilayer]"]
  C15 = Ceramic Capacitor [capacitance=100nF voltage=6.3V package="200 mil [THT, multilayer]"]
  C16 = Ceramic Capacitor [capacitance=100nF voltage=6.3V package="200 mil [THT, multilayer]"]
  C17 = Ceramic Capacitor [capacitance=100nF voltage=6.3V package="200 mil [THT, multilayer]"]
  74HCT08N = 74xx08 Logic AND Gate [part_number=74HC08 package="DIP (Dual Inline) [THT]"]
  PWR_A = Power Jack [package=power_jack_slot]
  PWR_B = female pin header, 2 pins [form="♀ (female)"]
  Microphone = KY-038

nets:
  GND: 1000_uf.-, Raspberry_Pi_Zero1.GND, J1.pin3, J2.pin3, J3.pin3, J4.pin3, J5.pin3, J6.pin3, J7.pin3, J8.pin3, J9.pin3, J10.pin3, J11.pin3, J12.pin3, J13.pin3, J14.pin3, J15.pin3, J16.pin3, J17.pin3, J18.pin3, J19.pin3, J20.pin3, J21.pin3, J22.pin3, J23.pin3, J24.pin3, C18.1, C1.1, C2.1, C19.1, C20.1, C21.1, C22.1, C23.1, C24.1, C3.1, C4.1, C5.1, C6.1, C7.1, C8.1, C9.1, C10.1, C11.1, C12.1, C13.1, C14.1, C15.1, C16.1, C17.1, 74HCT08N.GND, PWR_A.GND, PWR_B.pin2, Microphone.pin2
  5V: 1000_uf.+, Raspberry_Pi_Zero1.5V, J1.pin2, J2.pin2, J3.pin2, J4.pin2, J5.pin2, J6.pin2, J7.pin2, J8.pin2, J9.pin2, J10.pin2, J11.pin2, J12.pin2, J13.pin2, J14.pin2, J15.pin2, J16.pin2, J17.pin2, J18.pin2, J19.pin2, J20.pin2, J21.pin2, J22.pin2, J23.pin2, J24.pin2, C18.0, C1.0, C2.0, C19.0, C20.0, C21.0, C22.0, C23.0, C24.0, C3.0, C4.0, C5.0, C6.0, C7.0, C8.0, C9.0, C10.0, C11.0, C12.0, C13.0, C14.0, C15.0, C16.0, C17.0, 74HCT08N.VCC, PWR_A.PWR, PWR_B.pin1
  N1: R330.Pin_0, 74HCT08N.2Y
  N2: R330.Pin_1, J1.pin1
  3V3: Raspberry_Pi_Zero1.3v3, Raspberry_Pi_Zero1.3V3, Microphone.pin3
  N3: Raspberry_Pi_Zero1.GPIO6, Microphone.pin4
  N4: Raspberry_Pi_Zero1.GPIO18, 74HCT08N.2A, 74HCT08N.2B
  N5: J1.pin4, J2.pin1
  N6: J2.pin4, J3.pin1
  N7: J3.pin4, J4.pin1
  N8: J4.pin4, J5.pin1
  N9: J5.pin4, J6.pin1
  N10: J6.pin4, J7.pin1
  N11: J7.pin4, J8.pin1
  N12: J8.pin4, J9.pin1
  N13: J9.pin4, J10.pin1
  N14: J10.pin4, J11.pin1
  N15: J11.pin4, J12.pin1
  N16: J12.pin4, J13.pin1
  N17: J13.pin4, J14.pin1
  N18: J14.pin4, J15.pin1
  N19: J15.pin4, J16.pin1
  N20: J16.pin4, J17.pin1
  N21: J17.pin4, J18.pin1
  N22: J18.pin4, J19.pin1
  N23: J19.pin4, J20.pin1
  N24: J20.pin4, J21.pin1
  N25: J21.pin4, J22.pin1
  N26: J22.pin4, J23.pin1
  N27: J23.pin4, J24.pin1

notes:
  Neopixel Globe V4 R6
  VCC
  GND
  A0/GND/VCC/D0
  KY-038/VMA309

custom parts:
  Raspberry Pi Zero: The Raspberry Pi Zero is half the size of a Model A+, with twice the utility. A tiny Raspberry Pi that’s affordable enough for any project! · 1Ghz, Single-core CPU · 512MB RAM · Mini HDMI and USB On-The-Go ports · Micro USB power · HAT-compatible 40-pin header. In this version schematic has been changed so the pins match the GPIO connector. I.e. the left hand pins are all the pins (the power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
  74xx08 Logic AND Gate: IC containing quadruple 2-input positive-AND gates.
  KY-038: ky-038 Microphone sound sensor module
