# Fritzing sketch neopixel-globe-5 (saved by Fritzing 0.9.3b)
circuit board: 10.0013cm x 10.0013cm
breadboards: 1

parts:
  1000_uf = Electrolytic Capacitor [capacitance=1mF voltage=35V part_number="1000uF 25V 85C" package="200 mil [THT, electrolytic]"]
  R330 = Resistor [tolerance=±5% resistance=330 part_number=330 package=THT]
  Raspberry_Pi_Zero1 = Raspberry Pi Zero
  74HCT08N = 74xx08 Logic AND Gate [part_number=74HC08 package="DIP (Dual Inline) [THT]"]
  PWR_A = Power Jack [package=power_jack_slot]
  PWR_B = female pin header, 2 pins [form="♀ (female)"]
  Microphone = KY-038
  Part1 = 24 NeoPixel Ring [part_number=1586]

nets:
  GND: 1000_uf.-, Raspberry_Pi_Zero1.GND, 74HCT08N.GND, PWR_A.GND, PWR_B.pin2, Microphone.pin2, Part1.GND
  5V: 1000_uf.+, Raspberry_Pi_Zero1.5V, 74HCT08N.VCC, PWR_A.PWR, PWR_B.pin1, Part1.VDD
  N1: R330.Pin_0, 74HCT08N.2Y
  N2: R330.Pin_1, Part1.IN
  3V3: Raspberry_Pi_Zero1.3v3, Raspberry_Pi_Zero1.3V3, Microphone.pin3
  N3: Raspberry_Pi_Zero1.GPIO6, Microphone.pin4
  N4: Raspberry_Pi_Zero1.GPIO18, 74HCT08N.2A, 74HCT08N.2B

notes:
  Neopixel Globe V4 R6
  VCC
  GND
  A0/GND/VCC/D0
  KY-038/VMA309

custom parts:
  Raspberry Pi Zero: The Raspberry Pi Zero is half the size of a Model A+, with twice the utility. A tiny Raspberry Pi that’s affordable enough for any project! · 1Ghz, Single-core CPU · 512MB RAM · Mini HDMI and USB On-The-Go ports · Micro USB power · HAT-compatible 40-pin header. In this version schematic has been changed so the pins match the GPIO connector. I.e. the left hand pins are all the pins (the power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
  74xx08 Logic AND Gate: IC containing quadruple 2-input positive-AND gates.
  KY-038: ky-038 Microphone sound sensor module
  24 NeoPixel Ring: 24 ultra bright smart LED NeoPixels are arranged in a circle with 2.6" (66mm) outer diameter. The rings are 'chainable' - connect the output pin of one to the input pin of another. Use only one microcontroller pin to control as many as you can chain together! Each LED is addressable as the driver chip is inside the LED. Each one has ~18mA constant current drive so the color will be very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
